// Logisim project Part 1.circ as structural Verilog: 1 circuit, main circuit main
module main (
  input  A,
  input  B,
  input  C,
  input  A_2,
  input  B_2,
  input  C_2,
  input  A_3,
  input  B_3,
  input  C_3,
  output F,
  output F_2,
  output F_3
);

  wire and_1_out, and_2_out, and_3_out, and_4_out, and_5_out, not_1_out, not_2_out, not_3_out, not_4_out,
       not_5_out, not_6_out, not_7_out, not_8_out, not_9_out, or_1_out, or_2_out, or_3_out;

  not not_1 (not_1_out, A);
  not not_2 (not_2_out, B);
  not not_3 (not_3_out, C);
  not not_4 (not_4_out, A_2);
  not not_5 (not_5_out, B_2);
  not not_6 (not_6_out, C_2);
  not not_7 (not_7_out, A_3);
  not not_8 (not_8_out, B_3);
  not not_9 (not_9_out, C_3);
  and and_1 (and_1_out, A, C);
  and and_2 (and_2_out, not_1_out, not_2_out);
  and and_3 (and_3_out, not_1_out, not_3_out);
  or or_1 (or_1_out, not_5_out, not_6_out);
  and and_4 (and_4_out, A_2, C_2);
  and and_5 (and_5_out, not_4_out, or_1_out);
  or or_2 (or_2_out, A_3, not_8_out, not_9_out);
  or or_3 (or_3_out, not_7_out, C_3);
  or or_4 (F_2, and_4_out, and_5_out);
  or or_5 (F, and_1_out, and_2_out, and_3_out);
  and and_6 (F_3, or_2_out, or_3_out);

  // Notes on the sheet:
  //   1.
  //   2.
  //   3.
endmodule
