// Logisim project Part 2.circ as structural Verilog: 1 circuit, main circuit main
// A
module main (
  input  A,
  input  B,
  input  C,
  output X,
  output Y,
  output Z
);

  wire or_1_out;

  or or_1 (or_1_out, B, C);
  xor xor_1 (X, A, or_1_out);
  xor xor_2 (Y, B, C);

  assign Z = C;
endmodule
