// Logisim project Part1.circ as structural Verilog: 1 circuit, main circuit main
module main (
  input  Enable,
  input  [2:0] A_B_C,
  input  C1,
  input  C0,
  input  A,
  input  B,
  input  C,
  input  D,
  output S0,
  output S1,
  output S2,
  output S3,
  output S4,
  output S5,
  output S6,
  output S7,
  output out_17
);

  wire and_1_out, and_2_out, and_3_out, and_4_out, not_1_out, not_2_out;

  Decoder #(.select(3)) decoder_1 (
    .out0(S0), .out1(S1), .out2(S2), .out3(S3), .out4(S4), .out5(S5), .out6(S6), .out7(S7), .sel(A_B_C),
    .en(Enable));
  not not_1 (not_1_out, C1);
  not not_2 (not_2_out, C0);
  and and_1 (and_1_out, not_1_out, not_2_out, A);
  and and_2 (and_2_out, not_1_out, C0, B);
  and and_3 (and_3_out, C1, not_2_out, C);
  and and_4 (and_4_out, C1, D, C0);
  or or_1 (out_17, and_1_out, and_2_out, and_3_out, and_4_out);
endmodule
