// Logisim project Part2.circ as structural Verilog: 1 circuit, main circuit main
module main (
  input  [2:0] A_B_C,
  input  enable,
  input  in_3,
  input  in_4,
  input  in_5,
  input  in_6,
  input  in_7,
  input  in_8,
  input  enable_2,
  input  in_10,
  input  [2:0] A_B_C_2,
  input  in_12,
  output out_13,
  output out_14,
  output out_15,
  output out_16,
  output out_17,
  output out_18,
  output out_19,
  output out_20,
  output out_21
);

  Decoder #(.select(3)) decoder_1 (
    .out0(out_13), .out1(out_14), .out2(out_15), .out3(out_16), .out4(out_17), .out5(out_18), .out6(out_19),
    .out7(out_20), .sel(A_B_C), .en(enable));
  Multiplexer #(.select(3)) multiplexer_1 (
    .in0(in_3), .in1(in_4), .in2(in_5), .in3(in_6), .in4(in_7), .in5(in_8), .in6(in_10), .in7(in_12),
    .out(out_21), .sel(A_B_C_2), .en(enable_2));
endmodule
