// Logisim project Part3.circ as structural Verilog: 2 circuits, main circuit main
module main (
  input  N1,
  input  N0,
  output S0,
  output S1,
  output S2,
  output S3,
  output S4
);

  wire dec2x4_1_s0, dec2x4_1_s1;

  dec2x4 dec2x4_1 (.N1(N1), .N0(N0), .S0(dec2x4_1_s0), .S1(dec2x4_1_s1), .S2(S3), .S3(S4));
  or or_1 (S0, dec2x4_1_s0, S3);
  or or_2 (S1, S3, S2);
  or or_3 (S2, dec2x4_1_s0, dec2x4_1_s1);
endmodule

module dec2x4 (
  input  N1,
  input  N0,
  output S0,
  output S1,
  output S2,
  output S3
);

  wire not_1_out, not_2_out;

  not not_1 (not_1_out, N0);
  not not_2 (not_2_out, N1);
  and and_1 (S0, not_1_out, not_2_out, 1'b1);
  and and_2 (S1, not_2_out, N0, 1'b1);
  and and_3 (S2, N1, not_1_out, 1'b1);
  and and_4 (S3, N1, N0, 1'b1);
endmodule
