// Logisim project P3.circ as structural Verilog: 4 circuits, main circuit main
module main (
  input  [7:0] _7_6_5_4_3_2_1_0,
  output F,
  output G
);

  wire [2:0] subcircuit1_1_out_2;
  wire [3:3] undriven;

  subcircuit1 subcircuit1_1 (.in_1(_7_6_5_4_3_2_1_0), .out_2(subcircuit1_1_out_2));
  Hex_Digit_Display hex_digit_display_1 (.value({undriven[3], subcircuit1_1_out_2}));  // open: dp
  subcircuit2 subcircuit2_1 (.A(subcircuit1_1_out_2[0]), .B(subcircuit1_1_out_2[1]), .C(subcircuit1_1_out_2[2]), .F(F));
  LED Even_number (.in(F));
  subcircuit3 subcircuit3_1 (.A(subcircuit1_1_out_2[2]), .B(subcircuit1_1_out_2[1]), .C(subcircuit1_1_out_2[0]), .G(G));
  LED Odd_number_of_1_s (.in(G));
endmodule

module subcircuit1 (
  input  [7:0] in_1,
  output [2:0] out_2
);

  Priority_Encoder priority_encoder_1 (
    .in0(in_1[0]), .in1(in_1[1]), .in2(in_1[2]), .in3(in_1[3]), .in4(in_1[4]), .in5(in_1[5]), .in6(in_1[6]),
    .in7(in_1[7]), .out(out_2), .en_in(1'b1));  // open: gs, en_out
endmodule

// A B C
module subcircuit2 (
  input  A,
  input  B,
  input  C,
  output F
);

  wire not_1_out;

  not not_1 (not_1_out, A);
  Multiplexer #(.select(2)) multiplexer_1 (
    .in0(1'b0), .in1(not_1_out), .in2(not_1_out), .in3(not_1_out), .out(F), .sel({C, B}), .en(1'b1));
  LED led_1 (.in(F));
endmodule

module subcircuit3 (
  input  A,
  input  B,
  input  C,
  output G
);

  wire not_1_out;

  not not_1 (not_1_out, A);
  Multiplexer #(.select(2)) multiplexer_1 (
    .in0(A), .in1(not_1_out), .in2(not_1_out), .in3(A), .out(G), .sel({C, B}), .en(1'b1));
  LED led_1 (.in(G));
endmodule
