// Logisim project Part1.circ as structural Verilog: 1 circuit, main circuit main
// Clear
module main (
  input  Input_D,
  input  Input_J,
  input  Input_K,
  output Output_Q,
  output Output_Q_2
);

  wire Clear_2_out, Clear_out, Clock_2_out, Clock_out, Preset_2_out, Preset_out;

  Button Clock (.out(Clock_out));
  Button Clock_2 (.out(Clock_2_out));
  Button Preset (.out(Preset_out));
  Button Preset_2 (.out(Preset_2_out));
  D_Flip_Flop D_flip_flop (
    .clk(Clock_2_out), .D(Input_D), .Q(Output_Q), .preset(Preset_out), .en(1'b1), .reset(Clear_out));  // open: Qn
  Button Clear (.out(Clear_out));
  J_K_Flip_Flop JK_flip_flop (
    .J(Input_J), .clk(Clock_out), .K(Input_K), .Q(Output_Q_2), .preset(Preset_2_out), .en(1'b1),
    .reset(Clear_2_out));  // open: Qn
  Button Clear_2 (.out(Clear_2_out));
endmodule
