// Logisim project Part2.circ as structural Verilog: 1 circuit, main circuit main
module main (
  output Output_S1,
  output Output_So,
  output Output_S1_2,
  output Output_So_2,
  output Output_S1_3,
  output Output_So_3
);

  wire Clear_2_out, Clear_3_out, Clear_out, clock_2_out, clock_3_out, Clock_out, JK_flip_flop_3_qn,
       JK_flip_flop_qn, not_1_out, Preset_2_out, Preset_3_out, Preset_out;

  Button Clock (.out(Clock_out));
  not not_1 (not_1_out, Clock_out);
  Clock clock_2 (.out(clock_2_out));
  Button clock_3 (.out(clock_3_out));
  J_K_Flip_Flop JK_flip_flop (
    .J(1'b1), .clk(not_1_out), .K(1'b1), .Q(Output_So), .Qn(JK_flip_flop_qn), .preset(Preset_out), .en(1'b1),
    .reset(Clear_out));
  Button Preset (.out(Preset_out));
  J_K_Flip_Flop JK_flip_flop_2 (
    .J(1'b1), .clk(clock_3_out), .K(1'b1), .Q(Output_So_3), .preset(Preset_3_out), .en(1'b1),
    .reset(Clear_3_out));  // open: Qn
  Button Clear (.out(Clear_out));
  J_K_Flip_Flop JK_flip_flop_3 (
    .J(1'b1), .clk(clock_2_out), .K(1'b1), .Q(Output_So_2), .Qn(JK_flip_flop_3_qn), .preset(Preset_2_out),
    .en(1'b1), .reset(Clear_2_out));
  Button Preset_2 (.out(Preset_2_out));
  Button Preset_3 (.out(Preset_3_out));
  Button Clear_2 (.out(Clear_2_out));
  Button Clear_3 (.out(Clear_3_out));
  J_K_Flip_Flop JK_flip_flop_4 (
    .J(1'b1), .clk(JK_flip_flop_qn), .K(1'b1), .Q(Output_S1), .preset(Preset_out), .en(1'b1),
    .reset(Clear_out));  // open: Qn
  J_K_Flip_Flop JK_flip_flop_5 (
    .J(1'b1), .clk(JK_flip_flop_3_qn), .K(1'b1), .Q(Output_S1_2), .preset(Preset_2_out), .en(1'b1),
    .reset(Clear_2_out));  // open: Qn
  J_K_Flip_Flop JK_flip_flop_6 (
    .J(1'b1), .clk(Output_So_3), .K(1'b1), .Q(Output_S1_3), .preset(Preset_3_out), .en(1'b1),
    .reset(Clear_3_out));  // open: Qn

  // Notes on the sheet:
  //   b)
  //   a)
  //   Step-by-step simulation
  //   Simulation using a regular clock signal
endmodule
