// Logisim project Part3.circ as structural Verilog: 3 circuits, main circuit main
module main (
);

  wire Clear_out, clock_1_out, Preset_out;
  wire [1:0] c1_1_output_s1, c2_1_output_s1;

  Clock clock_1 (.out(clock_1_out));
  C1 c1_1 (
    .Clock(clock_1_out), .Preset(Preset_out), .Clear(Clear_out), .Output_S1(c1_1_output_s1[0]),
    .Output_So(c1_1_output_s1[1]));
  Button Preset (.out(Preset_out));
  C2 c2_1 (
    .Clock(clock_1_out), .Preset(Preset_out), .Clear(Clear_out), .Output_S1(c2_1_output_s1[0]),
    .Output_S0(c2_1_output_s1[1]));
  Button Clear (.out(Clear_out));
  LED led_1 (.in(c1_1_output_s1[0]));
  LED led_2 (.in(c2_1_output_s1[0]));
  Hex_Digit_Display hex_digit_display_1 (.value({2'b00, c1_1_output_s1}));  // open: dp
  Hex_Digit_Display hex_digit_display_2 (.value({2'b00, c2_1_output_s1}));  // open: dp

  // Notes on the sheet:
  //   No funciona bien
endmodule

module C1 (
  input  Clock,
  input  Clear,
  input  Preset,
  output Output_S1,
  output Output_So
);

  wire JK_flip_flop_qn;

  J_K_Flip_Flop JK_flip_flop (
    .J(1'b1), .clk(Clock), .K(1'b1), .Q(Output_So), .Qn(JK_flip_flop_qn), .preset(Preset), .en(1'b1),
    .reset(Clear));
  J_K_Flip_Flop JK_flip_flop_2 (
    .J(1'b1), .clk(JK_flip_flop_qn), .K(1'b1), .Q(Output_S1), .preset(Preset), .en(1'b1), .reset(Clear));  // open: Qn
  Hex_Digit_Display hex_digit_display_1 (.value({2'b00, Output_S1, Output_So}));  // open: dp
endmodule

module C2 (
  input  Clock,
  input  Preset,
  input  Clear,
  output Output_S1,
  output Output_S0
);

  J_K_Flip_Flop JK_flip_flop (
    .J(1'b1), .clk(Clock), .K(1'b1), .Q(Output_S0), .preset(Preset), .en(1'b1), .reset(Clear));  // open: Qn
  J_K_Flip_Flop JK_flip_flop_2 (
    .J(1'b1), .clk(Output_S0), .K(1'b1), .Q(Output_S1), .preset(Preset), .en(1'b1), .reset(Clear));  // open: Qn
  Hex_Digit_Display hex_digit_display_1 (.value({2'b00, Output_S1, Output_S0}));  // open: dp
endmodule
