// Logisim project P5.circ as structural Verilog: 1 circuit, main circuit main
module main (
  input  E
);

  wire and_1_out, and_2_out, and_3_out, button_1_out, clock_1_out, d_ff_1_qn, decoder_1_out0, decoder_1_out1,
       decoder_1_out2, decoder_1_out3, decoder_1_out8, decoder_1_out9, decoder_1_out12, decoder_1_out13,
       j_k_ff_1_qn, J_out, K_out, multiplexer_1_out, not_1_out, or_1_out, or_2_out;
  wire [2:0] j_k_ff_1_q;

  Clock clock_1 (.out(clock_1_out));
  Button button_1 (.out(button_1_out));
  not not_1 (not_1_out, E);
  and and_1 (and_1_out, j_k_ff_1_q[1], j_k_ff_1_q[0]);
  and and_2 (and_2_out, j_k_ff_1_q[0], E);
  and and_3 (and_3_out, d_ff_1_qn, not_1_out, j_k_ff_1_qn);
  or or_1 (or_1_out, j_k_ff_1_q[2], and_2_out, and_3_out, and_1_out);
  T_Flip_Flop t_ff_1 (
    .clk(clock_1_out), .T(or_1_out), .Q(j_k_ff_1_q[2]), .reset(button_1_out));  // open: Qn, preset, en
  Hex_Digit_Display hex_digit_display_1 (.value({1'b0, j_k_ff_1_q}));  // open: dp
  D_Flip_Flop d_ff_1 (
    .clk(clock_1_out), .D(j_k_ff_1_q[2]), .Q(j_k_ff_1_q[1]), .Qn(d_ff_1_qn), .reset(button_1_out));  // open: preset, en
  Decoder #(.select(4)) decoder_1 (
    .out0(decoder_1_out0), .out1(decoder_1_out1), .out2(decoder_1_out2), .out3(decoder_1_out3),
    .out8(decoder_1_out8), .out9(decoder_1_out9), .out12(decoder_1_out12), .out13(decoder_1_out13),
    .sel({E, j_k_ff_1_q}), .en(1'b1));  // open: out4, out5, out6, out7, out10, out11, out14, out15
  LED Q1 (.in(j_k_ff_1_q[1]));
  LED Q2 (.in(j_k_ff_1_q[2]));
  or J (J_out, decoder_1_out0, decoder_1_out2, decoder_1_out8, decoder_1_out12);
  or K (K_out, decoder_1_out1, decoder_1_out3, decoder_1_out9, decoder_1_out13);
  LED Q0 (.in(j_k_ff_1_q[0]));
  J_K_Flip_Flop j_k_ff_1 (
    .J(J_out), .clk(clock_1_out), .K(K_out), .Q(j_k_ff_1_q[0]), .Qn(j_k_ff_1_qn), .reset(button_1_out));  // open: preset, en
  or or_2 (or_2_out, j_k_ff_1_q[0], j_k_ff_1_q[1]);
  Multiplexer #(.select(2)) multiplexer_1 (
    .in0(d_ff_1_qn), .in1(1'b0), .in2(or_2_out), .in3(j_k_ff_1_qn), .out(multiplexer_1_out),
    .sel({E, j_k_ff_1_q[2]}), .en(1'b1));
  LED S (.in(multiplexer_1_out));

  // Notes on the sheet:
  //   ¿Por qué enable en 3??
  //   X=0 Sequence: 0,5,3,4,2,1,0...
  //   X=1 Sequence: 0,1,4,3,5,2,0...
  //   ¿Por qué??
endmodule
