// Logisim project Part1.circ as structural Verilog: 1 circuit, main circuit main
// m0
module main (
  input  E0,
  input  E1,
  input  E2,
  input  m1,
  input  m0,
  output out_6
);

  wire Clear_out, clock_1_out, multiplexer_1_out, multiplexer_2_out, multiplexer_3_out, Preset_out;
  wire [2:1] d_ff_2_q;

  Clock clock_1 (.out(clock_1_out));
  Button Clear (.out(Clear_out));
  Button Preset (.out(Preset_out));
  Hex_Digit_Display hex_digit_display_1 (.value({1'b0, E2, E1, E0}));  // open: dp
  Multiplexer #(.select(2)) multiplexer_1 (
    .in0(1'b0), .in1(E2), .in2(d_ff_2_q[2]), .in3(d_ff_2_q[1]), .out(multiplexer_1_out), .sel({m1, m0}));  // open: en
  D_Flip_Flop d_ff_1 (
    .clk(clock_1_out), .D(multiplexer_1_out), .Q(d_ff_2_q[2]), .preset(Preset_out), .reset(Clear_out));  // open: Qn, en
  Multiplexer #(.select(2)) multiplexer_2 (
    .in0(d_ff_2_q[2]), .in1(E1), .in2(d_ff_2_q[1]), .in3(out_6), .out(multiplexer_2_out), .sel({m1, m0}));  // open: en
  D_Flip_Flop d_ff_2 (
    .clk(clock_1_out), .D(multiplexer_2_out), .Q(d_ff_2_q[1]), .preset(Preset_out), .reset(Clear_out));  // open: Qn, en
  Multiplexer #(.select(2)) multiplexer_3 (
    .in0(d_ff_2_q[1]), .in1(E0), .in2(out_6), .in3(1'b0), .out(multiplexer_3_out), .sel({m1, m0}));  // open: en
  D_Flip_Flop d_ff_3 (
    .clk(clock_1_out), .D(multiplexer_3_out), .Q(out_6), .preset(Preset_out), .reset(Clear_out));  // open: Qn, en
  Hex_Digit_Display hex_digit_display_2 (.value({1'b0, d_ff_2_q, out_6}));  // open: dp
  LED led_1 (.in(out_6));

  // Notes on the sheet:
  //   Initial number
  //   D flipflops check the functionality
  //   Initial goes to the D FF, and depending on m0 and m1, it loads the number, shifts left or shofts rigth
  //   00 shift rigth
  //   0 1 Load
  //   1 0 stop
  //   1 1 shift left
endmodule
