// Logisim project Part2.circ as structural Verilog: 3 circuits, main circuit main
module main (
);

  wire [2:0] second_circuit_1_out_3;

  _2_bit_counter u_2_bit_counter_1 ();  // open: Q0, Q1
  Second_circuit second_circuit_1 (
    .out_3(second_circuit_1_out_3[0]), .out_4(second_circuit_1_out_3[1]), .out_5(second_circuit_1_out_3[2]));  // open: Q0, Q1
  Hex_Digit_Display hex_digit_display_1 (.value({1'b0, second_circuit_1_out_3}));  // open: dp
endmodule

module _2_bit_counter (
  output Q0,
  output Q1
);

  wire Clear_out, clock_1_out;

  Clock clock_1 (.out(clock_1_out));
  Button Clear (.out(Clear_out));
  T_Flip_Flop T0 (.clk(clock_1_out), .T(1'b1), .Q(Q0), .reset(Clear_out));  // open: Qn, preset, en
  T_Flip_Flop T1 (.clk(clock_1_out), .T(Q0), .Q(Q1), .reset(Clear_out));  // open: Qn, preset, en
  Hex_Digit_Display hex_digit_display_1 (.value({2'b00, Q1, Q0}));  // open: dp
endmodule

module Second_circuit (
  input  Q0,
  input  Q1,
  output out_3,
  output out_4,
  output out_5
);

  wire decoder_1_out1, decoder_1_out3;

  // NOT_Gate not_1 has open pins: in=Q0, out=open
  Decoder #(.select(2)) decoder_1 (
    .out0(out_3), .out1(decoder_1_out1), .out2(out_4), .out3(decoder_1_out3), .sel({Q1, Q0}), .en(1'b1));
  or or_1 (out_5, decoder_1_out1, decoder_1_out3);
endmodule
