// Logisim project CombinationalCircuits.circ as structural Verilog: 6 circuits, main circuit main
module main (
  input  A,
  input  B,
  input  C,
  input  D,
  output F
);

  wire subcircuito_2_1_f, subcircuito_2_2_1_f, subcircuito_2_3_1_f, subcircuito_3_1_1_out_5,
       subcircuito_3_2_1_f;

  Hex_Digit_Display hex_digit_display_1 (.value({3'b000, A}));  // open: dp
  Hex_Digit_Display hex_digit_display_2 (.value({3'b000, B}));  // open: dp
  Hex_Digit_Display hex_digit_display_3 (.value({3'b000, C}));  // open: dp
  Hex_Digit_Display hex_digit_display_4 (.value({3'b000, D}));  // open: dp
  Subcircuito_2_1 subcircuito_2_1 (.A(A), .B(B), .C(C), .D(D), .F(subcircuito_2_1_f));
  Subcircuito_3_1 subcircuito_3_1_1 (.D(A), .A(B), .B(C), .C(D), .out_5(subcircuito_3_1_1_out_5));
  Subcircuito_2_2 subcircuito_2_2_1 (.A(A), .B(B), .C(C), .D(D), .F(subcircuito_2_2_1_f));
  Subcircuito_2_3 subcircuito_2_3_1 (.A(A), .B(B), .C(C), .D(D), .F(subcircuito_2_3_1_f));
  Subcircuito_3_2 subcircuito_3_2_1 (.A(A), .B(B), .C(C), .D(D), .F(subcircuito_3_2_1_f));
  or or_1 (F, subcircuito_2_1_f, subcircuito_2_2_1_f, subcircuito_2_3_1_f, subcircuito_3_1_1_out_5, subcircuito_3_2_1_f);
endmodule

module Subcircuito_2_1 (
  input  A,
  input  B,
  input  C,
  input  D,
  output F
);

  wire and_1_out, and_2_out, and_3_out, and_4_out, and_5_out, not_1_out, not_2_out, not_3_out, not_4_out;

  not not_1 (not_1_out, A);
  not not_2 (not_2_out, B);
  not not_3 (not_3_out, C);
  not not_4 (not_4_out, D);
  and and_1 (and_1_out, not_1_out, not_2_out, C, not_4_out);
  and and_2 (and_2_out, A, not_2_out, not_3_out, not_4_out);
  and and_3 (and_3_out, C, B, A);
  and and_4 (and_4_out, A, C, D);
  and and_5 (and_5_out, not_1_out, B, D);
  or or_1 (F, and_1_out, and_2_out, and_3_out, and_4_out, and_5_out);

  // Notes on the sheet:
  //   F(A,B,C,D)=(A'B'CD')+(AB'C'D')+(A'BD)+(ABC)+(ACD)
endmodule

module Subcircuito_2_2 (
  input  A,
  input  B,
  input  C,
  input  D,
  output F
);

  wire nor_1_out, nor_2_out, nor_3_out, nor_4_out, nor_5_out, nor_6_out, nor_7_out, not_1_out, not_2_out,
       not_3_out, not_4_out;

  not not_1 (not_1_out, A);
  not not_2 (not_2_out, B);
  not not_3 (not_3_out, C);
  not not_4 (not_4_out, D);
  nor nor_1 (nor_1_out, A, B, C);
  nor nor_2 (nor_2_out, A, B, not_4_out);
  nor nor_3 (nor_3_out, A, not_2_out, not_3_out, D);
  nor nor_4 (nor_4_out, not_1_out, B, not_3_out, D);
  nor nor_5 (nor_5_out, not_2_out, D, C);
  nor nor_6 (nor_6_out, not_1_out, not_2_out, C);
  nor nor_7 (nor_7_out, not_4_out, C, not_1_out);
  nor nor_8 (F, nor_1_out, nor_2_out, nor_3_out, nor_4_out, nor_5_out, nor_6_out, nor_7_out);

  // Notes on the sheet:
  //   F(A,B,C,D)=(A+B+C)(A+B+D’)(A+B’+C’+D)(A’+B+C’+D)(B’+C+D)(A’+B’+C)(A’+C+D’)
endmodule

module Subcircuito_2_3 (
  input  A,
  input  B,
  input  C,
  input  D,
  output F
);

  wire decoder_1_out2, decoder_1_out5, decoder_1_out7, decoder_1_out8, decoder_1_out11, decoder_1_out14,
       decoder_1_out15, or_1_out, or_2_out;

  Decoder #(.select(4)) decoder_1 (
    .out2(decoder_1_out2), .out5(decoder_1_out5), .out7(decoder_1_out7), .out8(decoder_1_out8),
    .out11(decoder_1_out11), .out14(decoder_1_out14), .out15(decoder_1_out15), .sel({A, B, C, D}), .en(1'b1));  // open: out0, out1, out3, out4, out6, out9, out10, out12, out13
  or or_1 (or_1_out, decoder_1_out2, decoder_1_out5, decoder_1_out7);
  or or_2 (or_2_out, decoder_1_out8, decoder_1_out11, decoder_1_out14);
  or or_3 (F, or_1_out, or_2_out, decoder_1_out15);

  // Notes on the sheet:
  //   F=m2+m5+m7+m8+m11+m14+m15
endmodule

module Subcircuito_3_1 (
  input  D,
  input  A,
  input  B,
  input  C,
  output out_5
);

  wire not_1_out;

  not not_1 (not_1_out, D);
  Multiplexer #(.select(3)) multiplexer_1 (
    .in0(1'b0), .in1(not_1_out), .in2(D), .in3(D), .in4(not_1_out), .in5(D), .in6(1'b0), .in7(1'b1),
    .out(out_5), .sel({A, B, C}), .en(1'b1));
endmodule

module Subcircuito_3_2 (
  input  A,
  input  B,
  input  C,
  input  D,
  output F
);

  wire decoder_1_out0, decoder_1_out1, decoder_1_out2, decoder_1_out3, decoder_2_out2, decoder_3_out1,
       decoder_3_out3, decoder_4_out0, decoder_4_out3, decoder_5_out2, decoder_5_out3, or_1_out, or_2_out,
       or_3_out;

  Decoder #(.select(2), .disabled(0)) decoder_1 (
    .out0(decoder_1_out0), .out1(decoder_1_out1), .out2(decoder_1_out2), .out3(decoder_1_out3), .sel({A, B}),
    .en(1'b1));
  Decoder #(.select(2), .disabled(0)) decoder_2 (
    .out2(decoder_2_out2), .sel({C, D}), .en(decoder_1_out0));  // open: out0, out1, out3
  Decoder #(.select(2), .disabled(0)) decoder_3 (
    .out1(decoder_3_out1), .out3(decoder_3_out3), .sel({C, D}), .en(decoder_1_out1));  // open: out0, out2
  Decoder #(.select(2), .disabled(0)) decoder_4 (
    .out0(decoder_4_out0), .out3(decoder_4_out3), .sel({C, D}), .en(decoder_1_out2));  // open: out1, out2
  Decoder #(.select(2), .disabled(0)) decoder_5 (
    .out2(decoder_5_out2), .out3(decoder_5_out3), .sel({C, D}), .en(decoder_1_out3));  // open: out0, out1
  or or_1 (or_1_out, decoder_3_out1, decoder_3_out3);
  or or_2 (or_2_out, decoder_4_out0, decoder_4_out3);
  or or_3 (or_3_out, decoder_5_out2, decoder_5_out3);
  or or_4 (F, decoder_2_out2, or_1_out, or_2_out, or_3_out);
endmodule
