// Logisim project SequentialCircuits.circ as structural Verilog: 4 circuits, main circuit main
module main (
);

  wire clock_out, inicio_out;
  wire [2:0] cont_q0;
  wire [3:0] deco_s0, let_l0;

  Button inicio (.out(inicio_out));
  Clock clock (.out(clock_out));
  Cont_mod_7 cont (.Inicio(inicio_out), .Reloj(clock_out), .Q2(cont_q0[2]), .Q1(cont_q0[1]), .Q0(cont_q0[0]));
  Hex_Digit_Display hex_digit_display_1 (.value({1'b0, cont_q0}));  // open: dp
  Circ_deco deco (
    .Q2(cont_q0[2]), .Q1(cont_q0[1]), .Q0(cont_q0[0]), .S3(deco_s0[3]), .S2(deco_s0[2]), .S1(deco_s0[1]),
    .S0(deco_s0[0]));
  Hex_Digit_Display hex_digit_display_2 (.value(deco_s0));  // open: dp
  Letra \let  (
    .S3(deco_s0[3]), .S2(deco_s0[2]), .S1(deco_s0[1]), .S0(deco_s0[0]), .L3(let_l0[3]), .L2(let_l0[2]),
    .L1(let_l0[1]), .L0(let_l0[0]));
  Hex_Digit_Display hex_digit_display_3 (.value(let_l0));  // open: dp
endmodule

module Cont_mod_7 (
  input  Inicio,
  input  Reloj,
  output Q2,
  output Q1,
  output Q0
);

  wire and_1_out, and_2_out, and_3_out, nor_1_out, or_1_out, or_2_out;

  or or_1 (or_1_out, Q2, Q0);
  and and_1 (and_1_out, or_1_out, Q1);
  T_Flip_Flop t_ff_1 (.clk(Reloj), .T(and_1_out), .Q(Q2), .reset(Inicio));  // open: Qn, preset, en
  and and_2 (and_2_out, Q2, Q1);
  T_Flip_Flop t_ff_2 (.clk(Reloj), .T(or_2_out), .Q(Q1), .reset(Inicio));  // open: Qn, preset, en
  or or_2 (or_2_out, and_2_out, Q0);
  and and_3 (and_3_out, Q2, Q1);
  D_Flip_Flop d_ff_1 (.clk(Reloj), .D(nor_1_out), .Q(Q0), .reset(Inicio));  // open: Qn, preset, en
  nor nor_1 (nor_1_out, and_3_out, Q0);
  Hex_Digit_Display hex_digit_display_1 (.value({1'b0, Q2, Q1, Q0}));  // open: dp
endmodule

module Circ_deco (
  input  Q2,
  input  Q1,
  input  Q0,
  output S3,
  output S2,
  output S1,
  output S0
);

  wire and_2_out, and_3_out, and_4_out, and_5_out, and_6_out, not_1_out, not_2_out;

  not not_1 (not_1_out, Q0);
  and and_1 (S3, Q2, not_1_out);
  and and_2 (and_2_out, Q2, Q0);
  not not_2 (not_2_out, Q2);
  and and_3 (and_3_out, not_2_out, Q1, not_1_out);
  and and_4 (and_4_out, Q2, Q0);
  and and_5 (and_5_out, Q2, Q1);
  and and_6 (and_6_out, Q0, Q1);
  or or_1 (S2, and_2_out, and_3_out);
  xnor xnor_1 (S1, Q2, Q0);
  or or_2 (S0, and_4_out, and_5_out, and_6_out);
endmodule

module Letra (
  input  S3,
  input  S2,
  input  S1,
  input  S0,
  output L3,
  output L2,
  output L1,
  output L0
);

  wire not_1_out, not_2_out, not_3_out, or_1_out, or_2_out, or_3_out;

  not not_1 (not_1_out, S1);
  or or_1 (or_1_out, not_1_out, S2);
  not not_2 (not_2_out, S0);
  or or_2 (or_2_out, not_2_out, S2, S3);
  not not_3 (not_3_out, S2);
  or or_3 (or_3_out, not_3_out, S0, S1);
  nor nor_1 (L0, S3, S2, S1, S0);
  and and_1 (L2, or_1_out, or_2_out, or_3_out);

  assign L1 = 1'b1;
  assign L3 = 1'b1;
endmodule
