// Logisim project pr3_sol.circ as structural Verilog: 4 circuits, main circuit main
module main (
  input  [7:0] _7_6_5_4_3_2_1_0,
  output F,
  output G
);

  wire [2:0] circuito1_1_out_2;

  Circuito1 circuito1_1 (._7_6_5_4_3_2_1_0(_7_6_5_4_3_2_1_0), .out_2(circuito1_1_out_2));
  Hex_Digit_Display hex_digit_display_1 (.value({1'b0, circuito1_1_out_2}));  // open: dp
  Circuito2 circuito2_1 (.A(circuito1_1_out_2[2]), .B(circuito1_1_out_2[1]), .C(circuito1_1_out_2[0]), .F(F));
  LED led_1 (.in(F));
  Circuito3 circuito3_1 (.B(circuito1_1_out_2[1]), .C(circuito1_1_out_2[0]), .A(circuito1_1_out_2[2]), .out_4(G));
  LED led_2 (.in(G));

  // Notes on the sheet:
  //   ENTRADA
  //   SUBCIRCUIT0 1
  //   INDICE BIT PRIORITARIO
  //   SUBCIRCUITO 2
  //   A B C
  //   NÚMERO PAR
  //   SUBCIRCUITO 3
  //   B
  //   C
  //   A
  //   NÚMERO IMPAR DE UNOS
endmodule

module Circuito1 (
  input  [7:0] _7_6_5_4_3_2_1_0,
  output [2:0] out_2
);

  Priority_Encoder priority_encoder_1 (
    .in0(_7_6_5_4_3_2_1_0[0]), .in1(_7_6_5_4_3_2_1_0[1]), .in2(_7_6_5_4_3_2_1_0[2]),
    .in3(_7_6_5_4_3_2_1_0[3]), .in4(_7_6_5_4_3_2_1_0[4]), .in5(_7_6_5_4_3_2_1_0[5]),
    .in6(_7_6_5_4_3_2_1_0[6]), .in7(_7_6_5_4_3_2_1_0[7]), .out(out_2), .en_in(1'b1));  // open: gs, en_out

  // Notes on the sheet:
  //   INDICE BIT PRIORITARIO
endmodule

module Circuito2 (
  input  A,
  input  B,
  input  C,
  output F
);

  wire not_1_out;

  not not_1 (not_1_out, C);
  Multiplexer #(.select(2)) multiplexer_1 (
    .in0(1'b0), .in1(not_1_out), .in2(not_1_out), .in3(not_1_out), .out(F), .sel({B, A}), .en(1'b1));
  LED led_1 (.in(F));

  // Notes on the sheet:
  //   NUMERO PAR
endmodule

module Circuito3 (
  input  B,
  input  C,
  input  A,
  output out_4
);

  wire not_1_out, xor_1_out;

  xor xor_1 (xor_1_out, B, C);
  not not_1 (not_1_out, xor_1_out);
  Multiplexer #(.disabled(0), .enable("false")) multiplexer_1 (.in0(xor_1_out), .in1(not_1_out), .out(out_4), .sel(A));
  LED led_1 (.in(out_4));

  // Notes on the sheet:
  //   NUMERO IMPAR DE UNOS
endmodule
