// Logisim project pr4_sol.circ as structural Verilog: 5 circuits, main circuit main
module main (
);

  wire Inicio_out, Reloj_out;
  wire [1:0] c1_1_q0a, c2_1_q0d;

  Clock Reloj (.out(Reloj_out));
  Button Inicio (.out(Inicio_out));
  C1 c1_1 (
    .Reloj(Reloj_out), .CL0(Inicio_out), .CL1(Inicio_out), .Q0A(c1_1_q0a[0]), .Q1A(c1_1_q0a[1]));  // open: PR0, PR1
  C2 c2_1 (
    .Reloj(Reloj_out), .CL0(Inicio_out), .PR1(Inicio_out), .Q0D(c2_1_q0d[0]), .Q1D(c2_1_q0d[1]));  // open: PR0, CL1
  Hex_Digit_Display hex_digit_display_1 (.value({2'b00, c1_1_q0a}));  // open: dp
  LED \Primera_opción  (.in(c1_1_q0a[0]));
  Hex_Digit_Display hex_digit_display_2 (.value({2'b00, c2_1_q0d}));  // open: dp
  LED \Segunda_opción  (.in(c2_1_q0d[0]));

  // Notes on the sheet:
  //   Ascendente
  //   desde 00
  //   Descendente
  //   desde 10
  //   PARTE 3
endmodule

// ASC
module Ascendente (
  input  Reloj,
  output Q0A,
  output Q1A
);

  wire Inicio_out, j_k_ff_1_qn, not_1_out;

  not not_1 (not_1_out, Reloj);
  Button Inicio (.out(Inicio_out));
  J_K_Flip_Flop j_k_ff_1 (
    .J(1'b1), .clk(not_1_out), .K(1'b1), .Q(Q0A), .Qn(j_k_ff_1_qn), .en(1'b1), .reset(Inicio_out));  // open: preset
  J_K_Flip_Flop j_k_ff_2 (
    .J(1'b1), .clk(j_k_ff_1_qn), .K(1'b1), .Q(Q1A), .en(1'b1), .reset(Inicio_out));  // open: Qn, preset
  Hex_Digit_Display hex_digit_display_1 (.value({2'b00, Q1A, Q0A}));  // open: dp

  // Notes on the sheet:
  //   Contador asíncrono ascendente de 2 bits
  //   con inicialización a 00
  //   (conmuta en flanco de bajada)
  //   Figura 2
  //   PARTE 2
endmodule

// DES
module Descendente (
  input  Reloj,
  output Q0D,
  output Q1D
);

  wire Inicio_out;

  Button Inicio (.out(Inicio_out));
  J_K_Flip_Flop j_k_ff_1 (.J(1'b1), .clk(Reloj), .K(1'b1), .Q(Q0D), .preset(Inicio_out), .en(1'b1));  // open: Qn, reset
  J_K_Flip_Flop j_k_ff_2 (.J(1'b1), .clk(Q0D), .K(1'b1), .Q(Q1D), .preset(Inicio_out), .en(1'b1));  // open: Qn, reset
  Hex_Digit_Display hex_digit_display_1 (.value({2'b00, Q1D, Q0D}));  // open: dp

  // Notes on the sheet:
  //   Contador asíncrono descendente de 2 bits
  //   con inicialización a 11
  //   (conmuta en flanco de subida)
  //   Figura 3
  //   PARTE 2
endmodule

module C1 (
  input  Reloj,
  input  PR0,
  input  CL0,
  input  PR1,
  input  CL1,
  output Q0A,
  output Q1A
);

  wire j_k_ff_1_qn;

  J_K_Flip_Flop j_k_ff_1 (
    .J(1'b1), .clk(Reloj), .K(1'b1), .Q(Q0A), .Qn(j_k_ff_1_qn), .preset(PR0), .en(1'b1), .reset(CL0));
  J_K_Flip_Flop j_k_ff_2 (
    .J(1'b1), .clk(j_k_ff_1_qn), .K(1'b1), .Q(Q1A), .preset(PR1), .en(1'b1), .reset(CL1));  // open: Qn
  Hex_Digit_Display hex_digit_display_1 (.value({2'b00, Q1A, Q0A}));  // open: dp

  // Notes on the sheet:
  //   Contador asíncrono ascendente de 2 bits
endmodule

module C2 (
  input  Reloj,
  input  PR0,
  input  CL0,
  input  PR1,
  input  CL1,
  output Q0D,
  output Q1D
);

  J_K_Flip_Flop j_k_ff_1 (.J(1'b1), .clk(Reloj), .K(1'b1), .Q(Q0D), .preset(PR0), .en(1'b1), .reset(CL0));  // open: Qn
  J_K_Flip_Flop j_k_ff_2 (.J(1'b1), .clk(Q0D), .K(1'b1), .Q(Q1D), .preset(PR1), .en(1'b1), .reset(CL1));  // open: Qn
  Hex_Digit_Display hex_digit_display_1 (.value({2'b00, Q1D, Q0D}));  // open: dp

  // Notes on the sheet:
  //   Contador asíncrono descendente de 2 bits
endmodule
