// Logisim project pr5_sol.circ as structural Verilog: 1 circuit, main circuit main
module main (
  input  E
);

  wire and_1_out, and_2_out, and_3_out, d_ff_1_qn, decoder_1_out0, decoder_1_out1, decoder_1_out2,
       decoder_1_out3, decoder_1_out8, decoder_1_out9, decoder_1_out12, decoder_1_out13, inicio_out,
       j_k_ff_1_qn, multiplexer_1_out, not_1_out, or_1_out, or_2_out, or_3_out, or_4_out, Reloj_out;
  wire [2:0] j_k_ff_1_q;

  Clock Reloj (.out(Reloj_out));
  Button inicio (.out(inicio_out));
  Hex_Digit_Display hex_digit_display_1 (.value({1'b0, j_k_ff_1_q}));  // open: dp
  and and_1 (and_1_out, j_k_ff_1_q[0], j_k_ff_1_q[1]);
  and and_2 (and_2_out, j_k_ff_1_q[0], E);
  and and_3 (and_3_out, not_1_out, d_ff_1_qn, j_k_ff_1_qn);
  or or_1 (or_1_out, j_k_ff_1_q[2], and_1_out, and_2_out, and_3_out);
  not not_1 (not_1_out, E);
  LED Q2 (.in(j_k_ff_1_q[2]));
  LED Q1 (.in(j_k_ff_1_q[1]));
  LED Q0 (.in(j_k_ff_1_q[0]));
  T_Flip_Flop t_ff_1 (.clk(Reloj_out), .T(or_1_out), .Q(j_k_ff_1_q[2]), .reset(inicio_out));  // open: Qn, preset, en
  Decoder #(.select(4), .enable("false")) decoder_1 (
    .out0(decoder_1_out0), .out1(decoder_1_out1), .out2(decoder_1_out2), .out3(decoder_1_out3),
    .out8(decoder_1_out8), .out9(decoder_1_out9), .out12(decoder_1_out12), .out13(decoder_1_out13),
    .sel({E, j_k_ff_1_q}));  // open: out4, out5, out6, out7, out10, out11, out14, out15
  D_Flip_Flop d_ff_1 (
    .clk(Reloj_out), .D(j_k_ff_1_q[2]), .Q(j_k_ff_1_q[1]), .Qn(d_ff_1_qn), .reset(inicio_out));  // open: preset, en
  or or_2 (or_2_out, decoder_1_out0, decoder_1_out2, decoder_1_out8, decoder_1_out12);
  or or_3 (or_3_out, decoder_1_out1, decoder_1_out3, decoder_1_out9, decoder_1_out13);
  J_K_Flip_Flop j_k_ff_1 (
    .J(or_2_out), .clk(Reloj_out), .K(or_3_out), .Q(j_k_ff_1_q[0]), .Qn(j_k_ff_1_qn), .reset(inicio_out));  // open: preset, en
  or or_4 (or_4_out, j_k_ff_1_q[0], j_k_ff_1_q[1]);
  Multiplexer #(.select(2), .enable("false")) multiplexer_1 (
    .in0(d_ff_1_qn), .in1(1'b0), .in2(or_4_out), .in3(j_k_ff_1_qn), .out(multiplexer_1_out),
    .sel({E, j_k_ff_1_q[2]}));
  LED S (.in(multiplexer_1_out));
endmodule
