// Logisim project pr6_parte1sol.circ as structural Verilog: 1 circuit, main circuit main
module main (
  input  E0,
  input  E1,
  input  E2,
  input  m1,
  input  m0
);

  wire Clear_out, multiplexer_1_out, multiplexer_2_out, multiplexer_3_out, Preset_out, Reloj_out;
  wire [2:0] d_ff_3_q;

  Clock Reloj (.out(Reloj_out));
  Button Clear (.out(Clear_out));
  Button Preset (.out(Preset_out));
  Hex_Digit_Display hex_digit_display_1 (.value({1'b0, E2, E1, E0}));  // open: dp
  Multiplexer #(.select(2), .enable("false")) multiplexer_1 (
    .in0(1'b0), .in1(E2), .in2(d_ff_3_q[2]), .in3(d_ff_3_q[1]), .out(multiplexer_1_out), .sel({m1, m0}));
  D_Flip_Flop d_ff_1 (
    .clk(Reloj_out), .D(multiplexer_1_out), .Q(d_ff_3_q[2]), .preset(Preset_out), .reset(Clear_out));  // open: Qn, en
  Multiplexer #(.select(2), .enable("false")) multiplexer_2 (
    .in0(d_ff_3_q[2]), .in1(E1), .in2(d_ff_3_q[1]), .in3(d_ff_3_q[0]), .out(multiplexer_2_out), .sel({m1, m0}));
  Multiplexer #(.select(2), .enable("false")) multiplexer_3 (
    .in0(d_ff_3_q[1]), .in1(E0), .in2(d_ff_3_q[0]), .in3(1'b0), .out(multiplexer_3_out), .sel({m1, m0}));
  D_Flip_Flop d_ff_2 (
    .clk(Reloj_out), .D(multiplexer_2_out), .Q(d_ff_3_q[1]), .preset(Preset_out), .reset(Clear_out));  // open: Qn, en
  D_Flip_Flop d_ff_3 (
    .clk(Reloj_out), .D(multiplexer_3_out), .Q(d_ff_3_q[0]), .preset(Preset_out), .reset(Clear_out));  // open: Qn, en
  LED led_1 (.in(d_ff_3_q[0]));
  Hex_Digit_Display hex_digit_display_2 (.value({1'b0, d_ff_3_q}));  // open: dp

  // Notes on the sheet:
  //   Dato entrada
  //   Control
  //   Dato de entrada
  //   0 1 Carga
  //   1 0 Mantenimiento
  //   0 0 Desplazamiento a derecha
  //   1 1 Desplazamiento a izquierda
  //   Dato almacenado
endmodule
