// Logisim project pr6_parte2sol.circ as structural Verilog: 3 circuits, main circuit main
module main (
);

  wire CONT_q_prime_0, Reloj_out, Reset_out;
  wire [1:0] CONT_q0;
  wire [2:0] COMB_s0;

  Clock Reloj (.out(Reloj_out));
  Button Reset (.out(Reset_out));
  Hex_Digit_Display hex_digit_display_1 (.value({2'b00, CONT_q0}));  // open: dp
  contador CONT (.Reloj(Reloj_out), .Reset(Reset_out), .Q1(CONT_q0[1]), .Q0(CONT_q0[0]), .Q_prime_0(CONT_q_prime_0));
  combinacional COMB (.Q1(CONT_q0[1]), .Q0(CONT_q0[0]), .S2(COMB_s0[2]), .S1(COMB_s0[1]), .S0(COMB_s0[0]));
  Hex_Digit_Display hex_digit_display_2 (.value({1'b0, COMB_s0}));  // open: dp
endmodule

module contador (
  input  Reloj,
  input  Reset,
  output Q1,
  output Q0,
  output Q_prime_0
);

  T_Flip_Flop T1 (.clk(Reloj), .T(Q0), .Q(Q1), .reset(Reset));  // open: Qn, preset, en
  T_Flip_Flop T0 (.clk(Reloj), .T(1'b1), .Q(Q0), .Qn(Q_prime_0), .reset(Reset));  // open: preset, en
  Hex_Digit_Display hex_digit_display_1 (.value({2'b00, Q1, Q0}));  // open: dp
endmodule

module combinacional (
  input  Q1,
  input  Q0,
  output S2,
  output S1,
  output S0
);

  wire not_1_out;

  not not_1 (not_1_out, Q0);
  and and_1 (S2, Q1, not_1_out);

  assign S0 = 1'b0;
  assign S1 = Q0;
endmodule
